// Logisim project proj_3.circ as structural Verilog
module main (
  input  x
);

  wire base_6_up_down_counter_1_out_3, base_6_up_down_counter_1_out_4, base_6_up_down_counter_1_out_5,
       base_10_to_base_6_counter_1_x, base_10_up_down_counter_1_a, base_10_up_down_counter_1_b,
       base_10_up_down_counter_1_c, base_10_up_down_counter_1_d, clock_1_out, dec_7seg_driver_1_a_2,
       dec_7seg_driver_1_b_2, dec_7seg_driver_1_c_2, dec_7seg_driver_1_d_2, dec_7seg_driver_1_e,
       dec_7seg_driver_1_f, dec_7seg_driver_1_g, dec_7seg_driver_2_a_2, dec_7seg_driver_2_b_2,
       dec_7seg_driver_2_c_2, dec_7seg_driver_2_d_2, dec_7seg_driver_2_e, dec_7seg_driver_2_f,
       dec_7seg_driver_2_g;

  _7_Segment_Display u_7_segment_display_1 (
    .g(dec_7seg_driver_1_g), .f(dec_7seg_driver_1_f), .a(dec_7seg_driver_1_a_2), .b(dec_7seg_driver_1_b_2),
    .e(dec_7seg_driver_1_e), .d(dec_7seg_driver_1_d_2), .c(dec_7seg_driver_1_c_2));  // open: dp
  dec_7seg_driver dec_7seg_driver_1 (
    .D(base_6_up_down_counter_1_out_3), .C(base_6_up_down_counter_1_out_4),
    .B(base_6_up_down_counter_1_out_5), .A(1'b0), .a_2(dec_7seg_driver_1_a_2), .b_2(dec_7seg_driver_1_b_2),
    .c_2(dec_7seg_driver_1_c_2), .d_2(dec_7seg_driver_1_d_2), .e(dec_7seg_driver_1_e),
    .f(dec_7seg_driver_1_f), .g(dec_7seg_driver_1_g));
  _7_Segment_Display u_7_segment_display_2 (
    .g(dec_7seg_driver_2_g), .f(dec_7seg_driver_2_f), .a(dec_7seg_driver_2_a_2), .b(dec_7seg_driver_2_b_2),
    .e(dec_7seg_driver_2_e), .d(dec_7seg_driver_2_d_2), .c(dec_7seg_driver_2_c_2));  // open: dp
  dec_7seg_driver dec_7seg_driver_2 (
    .D(base_10_up_down_counter_1_a), .C(base_10_up_down_counter_1_b), .B(base_10_up_down_counter_1_c),
    .A(base_10_up_down_counter_1_d), .a_2(dec_7seg_driver_2_a_2), .b_2(dec_7seg_driver_2_b_2),
    .c_2(dec_7seg_driver_2_c_2), .d_2(dec_7seg_driver_2_d_2), .e(dec_7seg_driver_2_e),
    .f(dec_7seg_driver_2_f), .g(dec_7seg_driver_2_g));
  base_10_to_base_6_counter base_10_to_base_6_counter_1 (
    .x2(x), .D(base_10_up_down_counter_1_a), .C(base_10_up_down_counter_1_b),
    .B(base_10_up_down_counter_1_c), .A(base_10_up_down_counter_1_d), .x(base_10_to_base_6_counter_1_x));
  base_6_up_down_counter base_6_up_down_counter_1 (
    .x(x), .out_3(base_6_up_down_counter_1_out_3), .out_4(base_6_up_down_counter_1_out_4),
    .out_5(base_6_up_down_counter_1_out_5), .in_2(base_10_to_base_6_counter_1_x));
  base_10_up_down_counter base_10_up_down_counter_1 (
    .in_1(x), .in_2(clock_1_out), .A(base_10_up_down_counter_1_a), .B(base_10_up_down_counter_1_b),
    .C(base_10_up_down_counter_1_c), .D(base_10_up_down_counter_1_d));
  Clock clock_1 (.out(clock_1_out));
endmodule

module base_10_up_down_counter (
  input  in_1,
  input  in_2,
  output A,
  output B,
  output C,
  output D
);

  wire and_1_out, and_2_out, and_3_out, and_4_out, and_5_out, and_6_out, and_7_out, and_8_out, D_qn,
       nor_1_out, nor_2_out, nor_3_out, nor_4_out, nor_5_out, not_1_out, not_2_out, not_3_out, not_4_out,
       not_5_out, not_6_out, not_7_out, not_8_out, not_9_out, not_10_out, not_11_out, not_12_out, not_13_out,
       or_1_out, or_2_out, or_3_out, or_4_out, or_5_out, or_6_out;

  not not_1 (not_1_out, in_1);
  not not_2 (not_2_out, A);
  not not_3 (not_3_out, B);
  nor nor_1 (nor_1_out, in_1, D, C, B, A);
  and and_1 (and_1_out, in_1, C, B, A);
  and and_2 (and_2_out, not_1_out, D, not_2_out);
  and and_3 (and_3_out, in_1, not_3_out, A);
  or or_1 (or_1_out, nor_1_out, and_1_out);
  S_R_Flip_Flop u_D (.S(or_1_out), .clk(in_2), .R(or_2_out), .Q(D), .Qn(D_qn));  // open: preset, reset, en
  or or_2 (or_2_out, and_2_out, and_3_out);
  not not_4 (not_4_out, D);
  nor nor_2 (nor_2_out, in_1, not_4_out, A);
  not not_5 (not_5_out, C);
  and and_4 (and_4_out, in_1, not_5_out, B, A);
  not not_6 (not_6_out, C);
  nor nor_3 (nor_3_out, in_1, not_6_out, B, A);
  and and_5 (and_5_out, in_1, C, B, A);
  or or_3 (or_3_out, nor_2_out, and_4_out);
  or or_4 (or_4_out, nor_3_out, and_5_out);
  S_R_Flip_Flop u_C (.S(or_3_out), .clk(in_2), .R(or_4_out), .Q(C));  // open: Qn, preset, reset, en
  not not_7 (not_7_out, C);
  nor nor_4 (nor_4_out, in_1, not_7_out, B, A);
  nor nor_5 (nor_5_out, in_1, not_8_out, A);
  not not_8 (not_8_out, D);
  not not_9 (not_9_out, D);
  and and_6 (and_6_out, in_1, not_9_out, not_10_out, A);
  not not_10 (not_10_out, B);
  not not_11 (not_11_out, in_1);
  and and_7 (and_7_out, not_11_out, B, not_12_out);
  not not_12 (not_12_out, A);
  and and_8 (and_8_out, in_1, B, A);
  or or_5 (or_5_out, nor_4_out, nor_5_out, and_6_out);
  or or_6 (or_6_out, and_7_out, and_8_out);
  S_R_Flip_Flop u_B (.S(or_5_out), .clk(in_2), .R(or_6_out), .Q(B));  // open: Qn, preset, reset, en
  not not_13 (not_13_out, A);
  S_R_Flip_Flop u_A (.S(not_13_out), .clk(in_2), .R(A), .Q(A));  // open: Qn, preset, reset, en
endmodule

module base_6_up_down_counter (
  input  x,
  input  in_2,
  output out_3,
  output out_4,
  output out_5
);

  wire and_1_out, and_2_out, and_3_out, and_4_out, and_5_out, and_6_out, B_qn, C_qn, nor_1_out, nor_2_out,
       not_1_out, not_2_out, not_3_out, not_4_out, not_5_out, not_6_out, not_7_out, not_8_out, not_9_out,
       or_1_out, or_2_out, or_3_out, or_4_out, s_r_ff_1_qn;

  nor nor_1 (nor_1_out, x, out_5, out_4, out_3);
  and and_1 (and_1_out, x, out_4, out_3);
  not not_1 (not_1_out, x);
  and and_2 (and_2_out, not_1_out, out_5, not_2_out);
  not not_2 (not_2_out, out_3);
  and and_3 (and_3_out, x, out_5, out_3);
  or or_1 (or_1_out, nor_1_out, and_1_out);
  or or_2 (or_2_out, and_2_out, and_3_out);
  S_R_Flip_Flop C (.S(or_1_out), .clk(in_2), .R(or_2_out), .Q(out_5), .Qn(C_qn));  // open: preset, reset, en
  not not_3 (not_3_out, x);
  not not_4 (not_4_out, out_3);
  not not_5 (not_5_out, x);
  and and_4 (and_4_out, not_5_out, out_5, not_6_out);
  not not_6 (not_6_out, out_3);
  not not_7 (not_7_out, x);
  and and_5 (and_5_out, not_7_out, out_4, not_8_out);
  not not_8 (not_8_out, out_3);
  and and_6 (and_6_out, x, out_4, out_3);
  nor nor_2 (nor_2_out, not_3_out, out_5, out_4, not_4_out);
  or or_3 (or_3_out, nor_2_out, and_4_out);
  or or_4 (or_4_out, and_5_out, and_6_out);
  S_R_Flip_Flop B (.S(or_3_out), .clk(in_2), .R(or_4_out), .Q(out_4), .Qn(B_qn));  // open: preset, reset, en
  not not_9 (not_9_out, out_3);
  S_R_Flip_Flop s_r_ff_1 (
    .S(not_9_out), .clk(in_2), .R(out_3), .Q(out_3), .Qn(s_r_ff_1_qn));  // open: preset, reset, en
endmodule

module base_10_to_base_6_counter (
  input  x2,
  input  D,
  input  C,
  input  B,
  input  A,
  output x
);

  wire and_1_out, and_2_out, not_1_out, not_2_out, not_3_out, not_4_out, not_5_out;

  not not_1 (not_1_out, D);
  not not_2 (not_2_out, C);
  not not_3 (not_3_out, B);
  not not_4 (not_4_out, A);
  not not_5 (not_5_out, x2);
  and and_1 (and_1_out, x2, not_1_out, not_2_out, not_3_out, not_4_out);
  and and_2 (and_2_out, not_5_out, D, A);
  or or_1 (x, and_1_out, and_2_out);
endmodule

module dec_7seg_driver (
  input  D,
  input  C,
  input  B,
  input  A,
  output a_2,
  output b_2,
  output c_2,
  output d_2,
  output e,
  output f,
  output g
);

  wire and_1_out, and_2_out, and_3_out, and_4_out, and_5_out, and_6_out, and_7_out, and_8_out, and_9_out,
       and_10_out, and_11_out, and_12_out, and_13_out, and_14_out, and_15_out, and_16_out, not_1_out,
       not_2_out, not_3_out, not_4_out;

  not not_1 (not_1_out, D);
  not not_2 (not_2_out, C);
  not not_3 (not_3_out, B);
  not not_4 (not_4_out, A);
  and and_1 (and_1_out, not_1_out, not_3_out);
  and and_2 (and_2_out, D, B);
  and and_3 (and_3_out, not_1_out, not_2_out);
  and and_4 (and_4_out, D, C);
  and and_5 (and_5_out, not_1_out, not_3_out);
  and and_6 (and_6_out, not_1_out, C);
  and and_7 (and_7_out, C, not_3_out);
  and and_8 (and_8_out, D, not_2_out, B);
  and and_9 (and_9_out, not_1_out, not_3_out);
  and and_10 (and_10_out, not_1_out, C);
  and and_11 (and_11_out, not_1_out, not_2_out);
  and and_12 (and_12_out, not_1_out, B);
  and and_13 (and_13_out, not_2_out, B);
  and and_14 (and_14_out, not_2_out, B);
  and and_15 (and_15_out, not_1_out, C);
  and and_16 (and_16_out, C, not_3_out);
  or or_1 (a_2, and_1_out, A, C, and_2_out);
  or or_2 (b_2, and_3_out, not_3_out, and_4_out);
  or or_3 (c_2, not_2_out, B, D);
  or or_4 (d_2, and_5_out, and_6_out, A, and_7_out, and_8_out);
  or or_5 (e, and_9_out, and_10_out);
  or or_6 (f, and_11_out, and_12_out, A, and_13_out);
  or or_7 (g, A, and_14_out, and_15_out, and_16_out);

  // Notes on the sheet:
  //   C'+B+D
  //   D'B'+D'C
  //   A+C'B+D'C+CB'
  //   D'B'+A+C+DB
  //   D'C'+B'+DC
  //   D'B'+D'C'+A+CB'+DC'B
  //   D'C'+D'B+A+C'B
endmodule
